# Fritzing sketch Infrared Thermometer (saved by Fritzing 0.9.3b)

parts:
  WeMos_D1_Mini1 = WeMos D1 Mini
  WeMos_D1_Mini_OLED_Shield1 = WeMos D1 Mini OLED Shield  # not connected
  R1 = Resistor [tolerance=±5% resistance=220k package=THT]
  Laser_Switch = Round Pushbutton
  Power_Switch = Toggle Switch [package=THT]
  TP1 = TP4056 [chip_label=TP4056 package="DIP (Dual Inline) [THT]"]
  18650_Battery = 18650 battery holder [package=battery-18650-kit]
  MLX90614 = TMP102 [package=sot563]
  5V_Laser_Pointer = LEDs [package=led10mm]

nets:
  3V3: WeMos_D1_Mini1.3V3, MLX90614.VCC
  N1: WeMos_D1_Mini1.5V, Power_Switch.L1
  N2: WeMos_D1_Mini1.A0, R1.Pin_1
  N3: WeMos_D1_Mini1.D1, MLX90614.SCL
  N4: WeMos_D1_Mini1.D2, MLX90614.SDA
  N5: WeMos_D1_Mini1.G, TP1.pin6, MLX90614.GND, 5V_Laser_Pointer.C
  N6: R1.Pin_0, TP1.pin4, 18650_Battery.+
  N7: Laser_Switch.leg0, Power_Switch.COM, TP1.pin3
  N8: Laser_Switch.leg1, 5V_Laser_Pointer.A
  N9: TP1.pin5, 18650_Battery.-

custom parts:
  TP4056: A DIP stand-in part for whatever IC you want. With 6 pins on a 300mil dual inline package (DIP) footprint.
  18650 battery holder: 18650 Battery Holder
