# Fritzing sketch Infrared-Thermometer-Model-D (saved by Fritzing 0.9.3b)

parts:
  WeMos_D1_Mini1 = WeMos D1 Mini
  WeMos_D1_Mini_OLED_Shield1 = WeMos D1 Mini OLED Shield  # not connected
  Laser_Switch = Round Pushbutton
  Power_Switch = Toggle Switch [package=THT]
  MLX90614 = TMP102 [package=sot563]
  5V_Laser_Pointer = LEDs [package=led10mm]
  R1 = Resistor [tolerance=±5% resistance=220k package=THT]
  3_2V = Battery Holders [package=battery-aa-panel]

nets:
  3V3: WeMos_D1_Mini1.3V3, MLX90614.VCC
  N1: WeMos_D1_Mini1.5V, Power_Switch.L1
  N2: WeMos_D1_Mini1.A0, R1.Pin_1
  N3: WeMos_D1_Mini1.D1, MLX90614.SCL
  N4: WeMos_D1_Mini1.D2, MLX90614.SDA
  N5: WeMos_D1_Mini1.G, MLX90614.GND
  N6: Laser_Switch.leg0, Power_Switch.COM, R1.Pin_0, 3_2V.+
  N7: Laser_Switch.leg1, 5V_Laser_Pointer.A
  N8: 5V_Laser_Pointer.C, 3_2V.-
